// Logisim project hriddholab.circ as structural Verilog: 1 circuit, main circuit main
module main (
  input  I4,
  input  I3,
  input  [1:0] S1S0,
  input  I2,
  input  I1
);

  wire clock_1_out, d_ff_1_q, d_ff_1_qn, d_ff_2_q, d_ff_2_qn, multiplexer_1_out, multiplexer_2_out;

  Multiplexer #(.select(2)) multiplexer_1 (
    .in0(d_ff_1_q), .in1(I4), .in2(d_ff_2_q), .in3(I3), .out(multiplexer_1_out), .sel(S1S0));
  Multiplexer #(.select(2)) multiplexer_2 (
    .in0(d_ff_2_q), .in1(d_ff_1_q), .in2(I1), .in3(I2), .out(multiplexer_2_out), .sel(S1S0));
  D_Flip_Flop d_ff_1 (.D(multiplexer_1_out), .clk(clock_1_out), .Q(d_ff_1_q), .Qn(d_ff_1_qn));  // open: preset, reset
  Clock clock_1 (.out(clock_1_out));
  D_Flip_Flop d_ff_2 (.D(multiplexer_2_out), .clk(clock_1_out), .Q(d_ff_2_q), .Qn(d_ff_2_qn));  // open: preset, reset
endmodule
